# Fritzing sketch schematic (saved by Fritzing 0.7.4b)
breadboards: 1

parts:
  Arduino1 = Arduino
  R4 = Resistor [tolerance=±5% resistance=1k package=THT]
  R5 = Resistor [tolerance=±5% resistance=470 package=THT]
  S1 = Pushbutton [package="[THT]"]
  S2 = Pushbutton [package="[THT]"]

nets:
  N1: Arduino1.D9, R4.Pin_1
  N2: Arduino1.D7, R5.Pin_1
  N3: Arduino1.D3, S1.Pin_3, S1.Pin_4
  N4: Arduino1.D2, S2.Pin_3, S2.Pin_4
  N5: R4.Pin_0, R5.Pin_0
  N6: S1.Pin_1, S1.Pin_2, S2.Pin_1, S2.Pin_2
